# Fritzing sketch moisture_sensore (saved by Fritzing 0.9.2b)

parts:
  Part1 = FC-28 Soil Hygrometer Module - Probe
  Part2 = FC-28 Soil Hygrometer Module
  Part3 = Arduino Uno (Rev3)

nets:
  N1: Part1.POS, Part2.POS
  N2: Part1.NEG, Part2.NEG
  VCC: Part2.VCC, Part3.5V
  GND: Part2.GND, Part3.GND
  N3: Part2.AO, Part3.A0

custom parts:
  FC-28 Soil Hygrometer Module - Probe: The FC-28 is a soil hygrometer module that uses the Texas Instruments LM393 comparator chip to provide an analog measurement of soil humidity.
  FC-28 Soil Hygrometer Module: The FC-28 is a soil hygrometer module that uses the Texas Instruments LM393 comparator chip to provide an analog measurement of soil humidity. The digital output is high when soil moisture is over a certain threshold, as determined by adjusting the potentiometer.
